# Fritzing sketch esp-media-control (saved by Fritzing 0.9.5d)

parts:
  M1 = ESP32-S3-DevKitC-1-N8R8-v1 [part_number=ESP32-S3-DevKitC-1-N8R8-v1]
  J1 = single row smd male pin header, 5 pins [form="♂ (male)"]
  Sensor2 = TTP223B Capacitive Touch Sensor Module
  RE1 = KY-040 Rotary encoder [package=THT]
  J2 = single row smd male pin header, 5 pins [form="♂ (male)"]
  Sensor3 = TTP223B Capacitive Touch Sensor Module
  Sensor4 = TTP223B Capacitive Touch Sensor Module

nets:
  N1: M1.pin_1, M1.pin_2, J2.pin5
  N2: M1.pin_10, RE1.SW
  N3: M1.pin_11, RE1.DT
  N4: M1.pin_12, RE1.CLK
  N5: M1.pin_16, Sensor2.SIG
  N6: M1.pin_17, Sensor3.SIG
  N7: M1.pin_18, Sensor4.SIG
  N8: M1.pin_22, M1.pin_44, J1.pin5
  N9: J1.pin1, RE1.GND
  N10: J1.pin2, Sensor4.GND
  N11: J1.pin3, Sensor3.GND
  N12: J1.pin4, Sensor2.GND
  N13: Sensor2.VCC, J2.pin4
  N14: RE1.Vcc, J2.pin1
  N15: J2.pin2, Sensor4.VCC
  N16: J2.pin3, Sensor3.VCC

custom parts:
  ESP32-S3-DevKitC-1-N8R8-v1: ESP32-S3-DevKitC-1-N8R8-v1 This module is 44pins long (2x22) and 11 pins width.
  TTP223B Capacitive Touch Sensor Module: The TTP223B capacitive touch sensor module uses the TTP223B IC. The appropriate voltage is approximately 2 to 5.5 volts.
  KY-040 Rotary encoder: KY-040 Rotary Encoder with switch on breakout borad from AZ Delivery
